// Logisim project DENSENASTELAB4.circ as structural Verilog
module ALU (
  input  [2:0] F,
  input  [31:0] A,
  input  [31:0] B,
  output [31:0] Y,
  output Zero
);

  wire comparator_1_lt;
  wire [31:0] AANDB, ADD_SUB, ALTB, AORB, F0_32, F0_32_XOR;

  assign F0_32 = {{31{F[0]}}, F[0]};  // Bit_Extender bit_extender_1
  assign AANDB = A & B;  // AND_Gate and_1, 32 bits wide
  assign AORB = A | B;  // OR_Gate or_1, 32 bits wide
  Comparator #(.width(32)) comparator_1 (.a(A), .b(B), .lt(comparator_1_lt));  // open: gt, eq
  assign ALTB = {{31{1'b0}}, comparator_1_lt};  // Bit_Extender bit_extender_2
  Adder #(.width(32)) adder_1 (.a(A), .b(F0_32_XOR), .out(ADD_SUB), .cin(F[0]));  // open: cout
  assign F0_32_XOR = F0_32 ^ B;  // XOR_Gate xor_1, 32 bits wide
  Multiplexer #(.select(3), .width(32)) multiplexer_1 (
    .in0(ADD_SUB), .in1(ADD_SUB), .in2(AANDB), .in3(AORB), .in5(ALTB), .out(Y), .sel(F));  // open: in4, in6, in7
  Comparator #(.mode("unsigned"), .width(32)) comparator_2 (.a(Y), .b({32{1'b0}}), .eq(Zero));  // open: gt, lt
endmodule

module Datapath (
  output [31:0] t2
);

  wire and_1_out, BR, CLK, controlunit_1_regwrite, SRC, Zero;
  wire [2:0] ALUC, rom_1_data_2;
  wire [3:0] rom_1_data;
  wire [7:0] adder_1_out, BROF, multiplexer_1_out, PC, shifter_1_out;
  wire [31:0] AluOut, ImmEx, multiplexer_2_out, R2, registerfile_1_rd1, rom_1_data_3;

  Clock clock_1 (.out(CLK));
  and and_1 (and_1_out, BR, Zero);
  Register u_PC (.D(multiplexer_1_out), .en(1'b1), .clk(CLK), .Q(PC));  // open: clr
  Multiplexer #(.width(8)) multiplexer_1 (.in0(adder_1_out), .in1(BROF), .out(multiplexer_1_out), .sel(and_1_out));
  Adder adder_1 (.a(8'h4), .b(PC), .out(adder_1_out), .cin(1'b0));  // open: cout
  // Probe on PC
  Shifter #(.shift("lr")) shifter_1 (.in(PC), .\dist (3'b010), .out(shifter_1_out));
  ROM #(.dataWidth(32)) rom_1 (
    .addr(shifter_1_out),
    .data({rom_1_data_3[31:28], rom_1_data_2, rom_1_data_3[24:12], rom_1_data, rom_1_data_3[7:0]}));
  // Probe on {rom_1_data_2, rom_1_data, 1'b0}
  Adder adder_2 (.a({rom_1_data_2, rom_1_data, 1'b0}), .b(PC), .out(BROF), .cin(1'b0));  // open: cout
  assign ImmEx = {{20{rom_1_data_3[31]}}, {rom_1_data_3[31:28], rom_1_data_2, rom_1_data_3[24:20]}};  // Bit_Extender bit_extender_1
  RegisterFile registerfile_1 (
    .WD3(AluOut), .CLK(CLK), .A2(rom_1_data_3[22:20]), .A1(rom_1_data_3[17:15]),
    .A3({rom_1_data[1:0], rom_1_data_3[7]}), .WE3(controlunit_1_regwrite), .RD1(registerfile_1_rd1),
    .RD2(R2), .T2(t2));
  ControlUnit controlunit_1 (
    .Instruction({rom_1_data_3[31:28], rom_1_data_2, rom_1_data_3[24:12], rom_1_data, rom_1_data_3[7:0]}),
    .Branch(BR), .ALUControl(ALUC), .RegWrite(controlunit_1_regwrite), .ALUSrc(SRC));
  Multiplexer #(.width(32)) multiplexer_2 (.in0(R2), .in1(ImmEx), .out(multiplexer_2_out), .sel(SRC));
  ALU alu_1 (.A(registerfile_1_rd1), .B(multiplexer_2_out), .F(ALUC), .Y(AluOut), .Zero(Zero));

  // Notes on the sheet:
  //   contents of rom_1 (hex, n*v repeats v):
  //   293 100393 2028663 500333 93 30863 7080b3 fff30313 fe000ae3 8393 fff28293 28463 fc000ee3 63
endmodule

module RegisterFile (
  input  CLK,
  input  [2:0] A1,
  input  [31:0] WD3,
  input  [2:0] A2,
  input  WE3,
  input  [2:0] A3,
  output [31:0] RD1,
  output [31:0] RD2,
  output [31:0] T2
);

  wire and_1_out, and_2_out, and_3_out, and_4_out, and_5_out, and_6_out, and_7_out, decoder_1_out0,
       decoder_1_out1, decoder_1_out2, decoder_1_out3, decoder_1_out4, decoder_1_out5, decoder_1_out6,
       decoder_1_out7;
  wire [31:0] register_1_q, register_2_q, register_3_q, register_4_q, register_5_q, register_6_q;

  Decoder #(.select(3)) decoder_1 (
    .out0(decoder_1_out0), .out1(decoder_1_out1), .out2(decoder_1_out2), .out3(decoder_1_out3),
    .out4(decoder_1_out4), .out5(decoder_1_out5), .out6(decoder_1_out6), .out7(decoder_1_out7), .sel(A3));  // open: en
  and and_1 (and_1_out, WE3, decoder_1_out1);
  and and_2 (and_2_out, WE3, decoder_1_out2);
  and and_3 (and_3_out, WE3, decoder_1_out3);
  and and_4 (and_4_out, WE3, decoder_1_out4);
  and and_5 (and_5_out, WE3, decoder_1_out5);
  and and_6 (and_6_out, WE3, decoder_1_out6);
  and and_7 (and_7_out, WE3, decoder_1_out7);
  Register #(.width(32)) register_1 (.D(WD3), .en(and_1_out), .clk(CLK), .Q(register_1_q));  // open: clr
  Register #(.width(32)) register_2 (.D(WD3), .en(and_2_out), .clk(CLK), .Q(register_2_q));  // open: clr
  Register #(.width(32)) register_3 (.D(WD3), .en(and_3_out), .clk(CLK), .Q(register_3_q));  // open: clr
  Register #(.width(32)) register_4 (.D(WD3), .en(and_4_out), .clk(CLK), .Q(register_4_q));  // open: clr
  Register #(.width(32)) register_5 (.D(WD3), .en(and_5_out), .clk(CLK), .Q(register_5_q));  // open: clr
  Register #(.width(32)) register_6 (.D(WD3), .en(and_6_out), .clk(CLK), .Q(register_6_q));  // open: clr
  Register #(.width(32)) register_7 (.D(WD3), .en(and_7_out), .clk(CLK), .Q(T2));  // open: clr
  ControlUnit controlunit_1 ();  // open: Instruction, Branch, ALUControl, RegWrite, ALUSrc
  Multiplexer #(.enable("true"), .select(3), .width(32)) multiplexer_1 (
    .in0({32{1'b0}}), .in1(register_1_q), .in2(register_2_q), .in3(register_3_q), .in4(register_4_q),
    .in5(register_5_q), .in6(register_6_q), .in7(T2), .out(RD1), .sel(A1));  // open: en
  Multiplexer #(.enable("true"), .select(3), .width(32)) multiplexer_2 (
    .in0({32{1'b0}}), .in1(register_1_q), .in2(register_2_q), .in3(register_3_q), .in4(register_4_q),
    .in5(register_5_q), .in6(register_6_q), .in7(T2), .out(RD2), .sel(A2));  // open: en
endmodule

module ControlUnit (
  input  [31:0] Instruction,
  output Branch,
  output [2:0] ALUControl,
  output RegWrite,
  output ALUSrc
);

  wire comparator_3_eq;

  Comparator #(.mode("unsigned"), .width(7)) comparator_1 (
    .a(Instruction[6:0]), .b(7'b1100011), .eq(Branch));  // open: gt, lt
  Comparator #(.mode("unsigned"), .width(7)) comparator_2 (
    .a(Instruction[6:0]), .b(7'b0010011), .eq(ALUSrc));  // open: gt, lt
  Comparator #(.mode("unsigned"), .width(7)) comparator_3 (
    .a(Instruction[6:0]), .b(7'b0110011), .eq(comparator_3_eq));  // open: gt, lt
  assign ALUControl = {{2{1'b0}}, Branch};  // Bit_Extender bit_extender_1
  or or_1 (RegWrite, ALUSrc, comparator_3_eq);
endmodule

module Tests (
  output [31:0] Y,
  output [3:0] out_2,
  output [7:0] out_3
);


  assign out_2 = 4'b0010;
  assign out_3 = 8'h22;
  assign Y = 32'hf4010207;

  // Notes on the sheet:
  //   binary values in Logisim. Convince yourself how the bits are displayed.
  //   Example 1: A simple example that illustrates how 32-bit values are displayed as 
  //   Example 2) An example of how to extract certain bits from a (in this case) 32-bit wire. Here we extract the bits 8..11 from the 32-bit wire.
  //   Example 3) Sometimes it is useful to extract bits from different position and the re-assemble them. In this case, we extract bits 8..11 and bits 15..18 and assemble them into an 8-bit wire.
endmodule
